# Fritzing sketch pcb (saved by Fritzing 0.9.3b)
circuit board: 6.50001cm x 5.64998cm
perfboards: 1

parts:
  J2 = shrouded pin header, 40 pins [form="♂ (shrouded male)"]
  74HCT08 = 74HC08 Logic AND Gate [part_number=74HCT08 package="DIP (Dual Inline) [THT]"]
  R1 = Resistor [tolerance=±5% resistance=220 package=THT]  # not connected
  ATTINY85 = attiny85 [package=dip]
  R2 = Resistor [tolerance=±5% resistance=220 package=THT]  # not connected
  LED1 = LED - 3mm [color="Red (633nm)" package="3 mm [THT]"]
  LED2 = LED - 3mm [color="Red (633nm)" package="3 mm [THT]"]
  R3 = Resistor [tolerance=±5% resistance=220 package=THT]
  ATTINY86 = attiny85 [package=dip]
  R4 = Resistor [tolerance=±5% resistance=220 package=THT]
  R5 = Resistor [tolerance=±5% resistance=220 package=THT]
  R6 = Resistor [tolerance=±5% resistance=220 package=THT]
  SW1 = DIP SWITCH [package=dipswitch-02]
  SW2 = DIP SWITCH [package=dipswitch-02]
  J13 = female pin header, 3 pins [form="♀ (female)"]
  J14 = female pin header, 2 pins [form="♀ (female)"]

nets:
  N1: J2.pin5, 74HCT08.GND, ATTINY85.Pin_4, LED1.cathode, LED2.cathode, R3.Pin_0, ATTINY86.Pin_4, R4.Pin_0, R5.Pin_0, R6.Pin_0, J13.pin3, J14.pin2
  N2: J2.pin9, ATTINY85.Pin_8, ATTINY86.Pin_8, SW1.1, SW1.2, SW2.1, SW2.2
  N3: J2.pin40, 74HCT08.VCC, J13.pin1, J14.pin1

notes:
  5v/GND
  5v/D0/GND
  GNDx8
  5vx8
  Output
  Input
  Neopixel Raspberry PI HAT version 4
